# Fritzing sketch Skripsi (saved by Fritzing 0.9.3b)
breadboards: 1

parts:
  U1 = ESP32S-HiLetgo [part_number=ESP32S-HiLetgo]
  Part1 = Jtron 1 Channel Optoisolated Relay Module [package=relay]
  Part2 = SRF05 Ultrasonic Rangefinder
  Part3 = SRF05 Ultrasonic Rangefinder
  Part4 = SRF05 Ultrasonic Rangefinder
  YL-83_-_Control_Board1 = YL-83 Rain Sensor - Control Board
  YL-83_-_Detection_Board1 = YL-83 Rain Sensor - Detection Board
  YF-S201_Flow_Meter1 = YF-S201 Water Flow Meter
  S1 = Momentary Switch [package=ksa_sealed_tac_switch]
  LCD1 = LCD screen
  LCM1602_IIC1 = LCM1602 IIC [part_number="LCM1602 IIC" chip_label="LCM1602 IIC" package="DIP (Dual Inline) [THT]"]

nets:
  N1: U1.GPIO25, Part4.Trig
  N2: U1.GPIO26, Part4.Echo
  N3: U1.GPIO27, Part3.Trig
  N4: U1.GPIO14, Part3.Echo
  N5: U1.GPIO12, Part2.Trig
  N6: U1.GPIO13, Part2.Echo
  N7: U1.GPIO2, YF-S201_Flow_Meter1.SIG
  N8: U1.GPIO4, YL-83_-_Control_Board1.DO
  N9: U1.GPIO16, Part1.IN1
  N10: U1.GPIO21, LCM1602_IIC1.SDA
  N11: U1.GPIO22, LCM1602_IIC1.SCL
  N12: U1.GPIO23, S1.1, S1.2
  VCC: Part1.VCC, Part2.VCC, Part3.VCC, Part4.VCC, YL-83_-_Control_Board1.VCC, YF-S201_Flow_Meter1.VCC, LCM1602_IIC1.VCC
  GND: Part1.GND, Part2.GND, Part3.GND, Part4.GND, YL-83_-_Control_Board1.GND, YF-S201_Flow_Meter1.GND, S1.3, S1.4, LCM1602_IIC1.GND
  N13: YL-83_-_Control_Board1.POS, YL-83_-_Detection_Board1.POS
  N14: YL-83_-_Control_Board1.NEG, YL-83_-_Detection_Board1.NEG
  VSS: LCD1.VSS, LCM1602_IIC1.VSS
  VDD: LCD1.VDD, LCM1602_IIC1.VDD
  N15: LCD1.V0, LCM1602_IIC1.V0
  N16: LCD1.RS, LCM1602_IIC1.RS
  N17: LCD1.R/W, LCM1602_IIC1.RW
  N18: LCD1.E, LCM1602_IIC1.E
  N19: LCD1.DB0, LCM1602_IIC1.D0
  N20: LCD1.DB1, LCM1602_IIC1.D1
  N21: LCD1.DB2, LCM1602_IIC1.D2
  N22: LCD1.DB3, LCM1602_IIC1.D3
  N23: LCD1.DB4, LCM1602_IIC1.D4
  N24: LCD1.DB5, LCM1602_IIC1.D5
  N25: LCD1.DB6, LCM1602_IIC1.D6
  N26: LCD1.DB7, LCM1602_IIC1.D7
  N27: LCD1.LED+, LCM1602_IIC1.A
  N28: LCD1.LED-, LCM1602_IIC1.K

custom parts:
  ESP32S-HiLetgo: HiLetgo ESP-WROOM-32 ESP32 ESP-32S Development Board 2.4GHz Dual-Mode WiFi + Bluetooth Dual Cores Microcontroller The ESP32 integrated with Antenna switches, RF Balun, power amplifiers, low-noise amplifiers, filters, and management modules, and the entire solution occupies the least area of PCB. 2.4 GHz Wi-Fi plus Bluetooth dual-mode chip, with TSMC Ultra-low power consumption 40nm technology,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
  YL-83 Rain Sensor - Control Board: The YL-83 is a rain sensor that has more resistance when dry and less resistance when wet. The module runs at 5V.
  YL-83 Rain Sensor - Detection Board: The YL-83 is a rain sensor that has more resistance when dry and less resistance when wet. The module runs at 5V.
  YF-S201 Water Flow Meter: The YF-S201 Flow Meter. The input voltage is 5V to 24V (DC).
  LCM1602 IIC: I2C-Module to use a 1602 or 2004 LCD on with the wire.h libory Serial LCD Modul
